# Fritzing sketch mouse_controller (saved by Fritzing 0.9.9b)
breadboards: 1

parts:
  Pro_Micro3 = Pro Micro  # not connected
  ENCODER1 = Rotary Encoder with Knob

nets:
  N1: ENCODER1.no_name_yet#2, ENCODER1.no_name_yet#5

custom parts:
  Pro Micro: The SparkFun Pro Micro is a complete USB-based microcontoller development system, in a very small footprint, capable of implementing many types of projects. All programming can be done via the USB port.
  Rotary Encoder with Knob: Rotary Encoder with 1/4" Shaft and Knob
